// Logisim project control_unit.circ as structural Verilog: 1 circuit, main circuit main
module main (
  input  [5:0] six_upper_bits_of_instr,
  output Reg_Dest,
  output Branch,
  output Mem_Read,
  output Mem_to_Reg,
  output [1:0] ALU_Op,
  output Mem_Write,
  output ALU_Src,
  output Reg_Write
);

  Comparator #(.width(6)) comparator_1 (.a(six_upper_bits_of_instr), .b({6{1'b0}}), .eq(ALU_Op[0]));  // open: gt, lt

  assign ALU_Op[1] = 1'b0;
  assign Reg_Dest = ALU_Op[0];
  assign Reg_Write = ALU_Op[0];

  // Other names for the same wires on the sheet: six_bit_in[5:0] = six_upper_bits_of_instr

  // Notes on the sheet:
  //   Input
  //   R_Type
  //   Outputs
endmodule
